// Logisim project tme1.circ as structural Verilog: 5 circuits, main circuit mon_xor
module mon_xor (
  input  a1,
  input  b1,
  output s
);

  wire and_1_out, and_2_out, not_1_out, not_2_out;

  not not_1 (not_1_out, b1);
  not not_2 (not_2_out, a1);
  and and_1 (and_1_out, a1, not_1_out);
  and and_2 (and_2_out, not_2_out, b1);
  or or_1 (s, and_1_out, and_2_out);
endmodule

module mux2_avec_mult (
  input  e0,
  input  e1,
  input  s,
  output out_4
);

  Multiplexer multiplexer_1 (.in0(e0), .in1(e1), .out(out_4), .sel(s));  // open: en
endmodule

module mux2_sans_mult (
  input  v,
  input  e0,
  input  e1,
  output s
);

  wire and_1_out, and_2_out, not_1_out;

  not not_1 (not_1_out, v);
  and and_1 (and_1_out, not_1_out, e0);
  and and_2 (and_2_out, v, e1);
  or or_1 (s, and_1_out, and_2_out);
endmodule

module mux4_sorties (
  input  cin,
  input  a3,
  input  a2,
  input  a1,
  input  a0,
  input  b3,
  input  b2,
  input  b1,
  input  b0,
  output s3,
  output s2,
  output s1,
  output s0
);

  mux2_sans_mult mux2_sans_mult_1 (.e0(a3), .e1(b3), .v(cin), .s(s3));
  mux2_sans_mult mux2_sans_mult_2 (.e0(a2), .e1(b2), .v(cin), .s(s2));
  mux2_sans_mult mux2_sans_mult_3 (.e0(a1), .e1(b1), .v(cin), .s(s1));
  mux2_sans_mult mux2_sans_mult_4 (.e0(a0), .e1(b0), .v(cin), .s(s0));
endmodule

module mux4_vrai (
  input  i0,
  input  e0,
  input  e2,
  input  i1,
  input  e1,
  input  e3,
  output s
);

  wire mux2_sans_mult_1_s, mux2_sans_mult_2_s;

  mux2_sans_mult mux2_sans_mult_1 (.e0(e0), .e1(e1), .v(i0), .s(mux2_sans_mult_1_s));
  mux2_sans_mult mux2_sans_mult_2 (.e0(e2), .e1(e3), .v(i0), .s(mux2_sans_mult_2_s));
  mux2_sans_mult mux2_sans_mult_3 (.e0(mux2_sans_mult_1_s), .e1(mux2_sans_mult_2_s), .v(i1), .s(s));
endmodule
