// Logisim project tme2.circ as structural Verilog: 3 circuits, main circuit addi_1_bit
module addi_1_bit (
  input  cin,
  input  a,
  input  b,
  output cout,
  output s
);

  wire and_1_out, and_2_out, xor_1_out;

  and and_1 (and_1_out, a, b);
  xor xor_1 (xor_1_out, a, b);
  and and_2 (and_2_out, cin, xor_1_out);
  or or_1 (cout, and_2_out, and_1_out);
  xor xor_2 (s, cin, xor_1_out);
endmodule

module addi_4_bits (
  input  a0,
  input  a1,
  input  a2,
  input  a3,
  input  b2,
  input  b3,
  input  b0,
  input  b1,
  output cout,
  output s0,
  output s1,
  output s2,
  output s3
);

  wire addi_1_bit_1_cout, addi_1_bit_2_cout, addi_1_bit_3_cout;

  addi_1_bit addi_1_bit_1 (.cin(1'b0), .a(a0), .b(b0), .cout(addi_1_bit_1_cout), .s(s0));
  addi_1_bit addi_1_bit_2 (.cin(addi_1_bit_1_cout), .a(a1), .b(b1), .cout(addi_1_bit_2_cout), .s(s1));
  addi_1_bit addi_1_bit_3 (.cin(addi_1_bit_2_cout), .a(a2), .b(b2), .cout(addi_1_bit_3_cout), .s(s2));
  addi_1_bit addi_1_bit_4 (.cin(addi_1_bit_3_cout), .a(a3), .b(b3), .cout(cout), .s(s3));
endmodule

module addi_soust_4_bits (
  input  a0,
  input  a1,
  input  a2,
  input  a3,
  input  Aluop,
  input  b0,
  input  b1,
  input  b2,
  input  b3,
  output cout,
  output s3,
  output s2,
  output s1,
  output s0
);

  wire addi_1_bit_1_cout, addi_1_bit_2_cout, addi_1_bit_3_cout, xor_1_out, xor_2_out, xor_3_out, xor_4_out;

  xor xor_1 (xor_1_out, Aluop, b0);
  addi_1_bit addi_1_bit_1 (.cin(Aluop), .a(a0), .b(xor_1_out), .cout(addi_1_bit_1_cout), .s(s0));
  xor xor_2 (xor_2_out, addi_1_bit_1_cout, b1);
  addi_1_bit addi_1_bit_2 (.cin(addi_1_bit_1_cout), .a(a1), .b(xor_2_out), .cout(addi_1_bit_2_cout), .s(s1));
  addi_1_bit addi_1_bit_3 (.cin(addi_1_bit_2_cout), .a(a2), .b(xor_3_out), .cout(addi_1_bit_3_cout), .s(s2));
  xor xor_3 (xor_3_out, addi_1_bit_2_cout, b2);
  xor xor_4 (xor_4_out, addi_1_bit_3_cout, b3);
  addi_1_bit addi_1_bit_4 (.cin(addi_1_bit_3_cout), .a(a3), .b(xor_4_out), .cout(cout), .s(s3));
endmodule
